// Logisim project prova.circ as structural Verilog: 1 circuit, main circuit main
module main (
  input  A,
  input  B,
  input  C,
  input  D,
  output S
);

  wire and_1_out, and_2_out, and_3_out, and_4_out, and_5_out;

  not not_1 (A, A);
  not not_2 (C, C);
  not not_3 (D, D);
  not not_4 (A, A);
  not not_5 (D, D);
  not not_6 (B, B);
  and and_1 (and_1_out, A, C, D);
  and and_2 (and_2_out, A, C, D);
  and and_3 (and_3_out, A, B, C);
  and and_4 (and_4_out, A, B, C);
  and and_5 (and_5_out, A, C, D);
  or or_1 (S, and_1_out, and_2_out, and_3_out, and_4_out, and_5_out);
endmodule
