// Logisim project prova2.circ as structural Verilog: 1 circuit, main circuit main
module main (
  input  A,
  input  B,
  input  C,
  input  D,
  output S
);

  wire or_1_out;

  not not_1 (A, A);
  not not_2 (C, C);
  not not_3 (D, D);
  or or_1 (or_1_out, A, B, C);
  and and_1 (S, D, or_1_out);
endmodule
