// Logisim project prova3.circ as structural Verilog: 1 circuit, main circuit main
module main (
  input  A,
  input  C,
  input  D,
  output S
);

  wire and_1_out, and_2_out;

  not not_1 (C, C);
  not not_2 (A, A);
  not not_3 (D, D);
  and and_1 (and_1_out, C, D);
  and and_2 (and_2_out, A, C, D);
  or or_1 (S, and_1_out, and_2_out);
endmodule
