// Logisim project prova4.circ as structural Verilog: 1 circuit, main circuit main
module main (
  input  S,
  input  R,
  output Q,
  output Qnegado
);

  wire C_out, nand_1_out, nand_2_out;

  Clock C (.out(C_out));
  nand nand_1 (nand_1_out, S, C_out);
  nand nand_2 (nand_2_out, C_out, R);
  nand nand_3 (Q, nand_1_out, Qnegado);
  nand nand_4 (Qnegado, Q, nand_2_out);
endmodule
